# Fritzing sketch H-Bridge (saved by Fritzing 0.8.3b)
breadboards: 1

parts:
  Teensy1 = Teensy 2.0
  IC1 = H-Bridge [package=THT]
  M1 = DC Motor

nets:
  GND: Teensy1.GND, IC1.GND1, IC1.GND2, IC1.GND3, IC1.GND4
  N1: Teensy1.D3, IC1.2A
  N2: Teensy1.C6, IC1.1A
  N3: Teensy1.C7, IC1.1_2EN
  N4: Teensy1.VCC, IC1.VCC2, IC1.VCC1
  N5: IC1.1Y, M1.pin_2
  N6: IC1.2Y, M1.pin_1

custom parts:
  Teensy 2.0: The Teensy is a complete USB-based microcontoller development system, in a very small footprint, capable of implementing many types of projects. All programming is done via the USB port. No special programmer is needed, only a standard "Mini-B" USB cable and a PC or Macintosh with a USB port.
